// Digital circuit DISPLAY RESULTADO.dig as structural Verilog
module DISPLAY_RESULTADO (
  input  Codi,
  input  R2,
  input  R1,
  input  R0,
  output d1,
  output d2,
  output d3,
  output d4,
  output d5,
  output d6,
  output d7
);

  wire and_1_out, and_2_out, and_3_out, and_4_out, and_5_out, and_6_out, and_7_out, and_8_out, and_9_out,
       and_10_out, and_11_out, and_12_out, and_13_out, and_14_out, and_15_out, and_17_out, and_18_out,
       and_19_out, and_20_out, not_1_out, not_2_out, not_3_out, not_4_out;

  not not_1 (not_1_out, Codi);
  not not_2 (not_2_out, R2);
  not not_3 (not_3_out, R1);
  not not_4 (not_4_out, R0);
  and and_1 (and_1_out, not_1_out, R0, not_3_out, R2);
  and and_2 (and_2_out, Codi, not_4_out);
  and and_3 (and_3_out, Codi, R1);
  and and_4 (and_4_out, not_4_out, not_2_out);
  and and_5 (and_5_out, not_4_out, R1);
  and and_6 (and_6_out, R1, not_2_out);
  or or_1 (d3, R0, not_3_out);
  and and_7 (and_7_out, not_1_out, R0, not_3_out, R2);
  and and_8 (and_8_out, Codi, not_4_out);
  and and_9 (and_9_out, Codi, R1);
  and and_10 (and_10_out, not_4_out, not_2_out);
  and and_11 (and_11_out, not_4_out, R1);
  and and_12 (and_12_out, R1, not_2_out);
  and and_13 (and_13_out, Codi, not_4_out);
  and and_14 (and_14_out, not_4_out, not_2_out);
  and and_15 (and_15_out, not_4_out, R1);
  and and_16 (d6, not_4_out, not_3_out);
  and and_17 (and_17_out, not_1_out, not_3_out, R2);
  and and_18 (and_18_out, Codi, R1);
  and and_19 (and_19_out, not_4_out, R1);
  and and_20 (and_20_out, R1, not_2_out);
  or or_2 (d5, and_13_out, and_14_out, and_15_out);
  or or_3 (d7, and_17_out, and_18_out, and_19_out, and_20_out);
  or or_4 (d1, and_1_out, and_2_out, and_3_out, and_4_out, and_5_out, and_6_out);
  or or_5 (d4, and_7_out, and_8_out, and_9_out, and_10_out, and_11_out, and_12_out);

  assign d2 = 1'b1;
endmodule
