// Digital circuit Resta C2.dig as structural Verilog
module Resta_C2 (
  input  A0,
  input  B0,
  input  A1,
  input  B1,
  input  B2,
  input  A2,
  output R0,
  output R1,
  output Cout,
  output R2,
  output Ov
);

  wire and_1_out, and_2_out, and_3_out, and_4_out, and_5_out, and_6_out, and_7_out, and_8_out, not_1_out,
       not_2_out, not_3_out, not_4_out, not_5_out, not_6_out, or_2_out, or_3_out, xor_1_out, xor_2_out,
       xor_3_out;

  not not_1 (not_1_out, B1);
  not not_2 (not_2_out, B0);
  not not_3 (not_3_out, B2);
  xor xor_1 (xor_1_out, A0, not_2_out);
  and and_1 (and_1_out, A1, not_1_out);
  xor xor_2 (xor_2_out, A1, not_1_out);
  and and_2 (and_2_out, A0, not_2_out);
  xor xor_3 (xor_3_out, A2, not_3_out);
  and and_3 (and_3_out, A2, not_3_out);
  not not_4 (not_4_out, R2);
  and and_4 (and_4_out, xor_1_out, 1'b1);
  xor xor_4 (R0, xor_1_out, 1'b1);
  and and_5 (and_5_out, xor_3_out, or_2_out);
  and and_6 (and_6_out, xor_2_out, or_3_out);
  xor xor_5 (R1, xor_2_out, or_3_out);
  xor xor_6 (R2, xor_3_out, or_2_out);
  not not_5 (not_5_out, A2);
  not not_6 (not_6_out, not_3_out);
  or or_1 (Cout, and_3_out, and_5_out);
  and and_7 (and_7_out, not_4_out, A2, not_3_out);
  and and_8 (and_8_out, R2, not_5_out, not_6_out);
  or or_2 (or_2_out, and_1_out, and_6_out);
  or or_3 (or_3_out, and_2_out, and_4_out);
  or or_4 (Ov, and_7_out, and_8_out);

  // Notes on the sheet:
  //   Carry In
endmodule
