// Digital circuit Circuit complet.dig as structural Verilog
module Circuit_complet (
  input  m_1,
  input  m_0,
  input  CLK,
  output Z_2,
  output Z_1,
  output Z_0
);

  wire and_1_out, and_2_out, and_3_out, and_4_out, and_5_out, and_6_out, and_7_out, and_8_out, and_9_out,
       and_10_out, and_11_out, and_12_out, and_13_out, not_1_out, not_2_out, not_3_out, not_4_out, not_5_out,
       or_1_out, or_2_out, or_3_out;

  not not_1 (not_1_out, m_1);
  not not_2 (not_2_out, m_0);
  not not_3 (not_3_out, Z_2);
  not not_4 (not_4_out, Z_1);
  not not_5 (not_5_out, Z_0);
  and and_1 (and_1_out, not_5_out, not_4_out, not_3_out, m_0, not_1_out);
  and and_2 (and_2_out, Z_0, Z_2, m_0, not_1_out);
  and and_3 (and_3_out, Z_0, Z_1, not_3_out, not_2_out);
  and and_4 (and_4_out, not_5_out, Z_1, Z_2);
  and and_5 (and_5_out, Z_1, m_0, m_1);
  and and_6 (and_6_out, not_4_out, Z_2, not_2_out);
  and and_7 (and_7_out, not_5_out, not_4_out, m_0, not_1_out);
  and and_8 (and_8_out, Z_0, not_4_out, not_2_out);
  and and_9 (and_9_out, not_5_out, Z_1, not_2_out);
  and and_10 (and_10_out, Z_0, Z_1, m_0);
  and and_11 (and_11_out, Z_0, m_0, m_1);
  and and_12 (and_12_out, not_5_out, not_1_out);
  and and_13 (and_13_out, not_5_out, not_2_out);
  or or_1 (or_1_out, and_7_out, and_8_out, and_9_out, and_10_out, and_11_out);
  or or_2 (or_2_out, and_12_out, and_13_out);
  or or_3 (or_3_out, and_1_out, and_2_out, and_3_out, and_4_out, and_5_out, and_6_out);
  D_FF D_2 (.D(or_3_out), .C(CLK), .Q(Z_2));  // open: nQ
  D_FF D_1 (.D(or_1_out), .C(CLK), .Q(Z_1));  // open: nQ
  D_FF D_0 (.D(or_2_out), .C(CLK), .Q(Z_0));  // open: nQ

  // Other names for the same wires on the sheet: z0 = Z_0; z1 = Z_1; z2 = Z_2

  // Notes on the sheet:
  //   CLK: Hz: 2
  //   M1=0,m0=0: BNSS ascendente
  //   M1=0,m0=1: BNSS descendente
  //   M1=1,m0=0: C2 ascendente
  //   M1=1,m0=1: desplazamiento a la izq 1 bit
  //   Entradas con respectivos modos de funcionamiento.
  //   Q_2
  //   Q_1
  //   Q_0
endmodule
