// Digital circuit Circuit complet.dig as structural Verilog
module Circuit_complet (
  input  B2,
  input  B1,
  input  B0,
  input  A0,
  input  A1,
  input  A2,
  input  Op,
  input  Codi,
  output out_9,
  output out_10,
  output R1,
  output R2,
  output R0
);

  wire and_1_out, and_2_out, and_3_out, and_4_out, and_5_out, and_6_out, and_7_out, and_8_out, and_9_out,
       and_10_out, and_11_out, and_12_out, and_13_out, and_14_out, and_15_out, and_16_out, and_17_out,
       and_18_out, and_19_out, and_20_out, and_21_out, and_22_out, and_23_out, and_24_out, and_25_out,
       and_26_out, and_27_out, and_28_out, display_entrada_a_1_d1, display_entrada_a_1_d2,
       display_entrada_a_1_d3, display_entrada_a_1_d4, display_entrada_a_1_d5, display_entrada_a_1_d6,
       display_entrada_a_1_d7, display_entrada_b_1_d1, display_entrada_b_1_d2, display_entrada_b_1_d3,
       display_entrada_b_1_d4, display_entrada_b_1_d5, display_entrada_b_1_d6, display_entrada_b_1_d7,
       display_resultado_1_d1, display_resultado_1_d2, display_resultado_1_d3, display_resultado_1_d4,
       display_resultado_1_d5, display_resultado_1_d6, display_resultado_1_d7, not_1_out, not_2_out,
       or_1_out, or_2_out, or_3_out, or_4_out, or_5_out, or_6_out, resta_c2_1_cout, resta_c2_1_ov,
       resta_c2_1_r0, resta_c2_1_r1, resta_c2_1_r2, resta_sm_1_c, resta_sm_1_o, resta_sm_1_r0, resta_sm_1_r1,
       resta_sm_1_r2, suma_c2_1_c, suma_c2_1_o, suma_c2_1_r0, suma_c2_1_r1, suma_c2_1_r2, suma_sm_1_c,
       suma_sm_1_o, suma_sm_1_r0, suma_sm_1_r1, suma_sm_1_r2;

  not not_1 (not_1_out, Codi);
  not not_2 (not_2_out, Op);
  and and_1 (and_1_out, not_2_out, not_1_out, 1'b1);
  and and_2 (and_2_out, not_2_out, Codi, 1'b1);
  and and_3 (and_3_out, Op, not_1_out, 1'b1);
  and and_4 (and_4_out, Op, Codi, 1'b1);
  Display_ENTRADA_A display_entrada_a_1 (
    .Codi(Codi), .A2(or_1_out), .A1(or_2_out), .A0(or_3_out), .d1(display_entrada_a_1_d1),
    .d2(display_entrada_a_1_d2), .d3(display_entrada_a_1_d3), .d4(display_entrada_a_1_d4),
    .d5(display_entrada_a_1_d5), .d6(display_entrada_a_1_d6), .d7(display_entrada_a_1_d7));
  and and_5 (and_5_out, A2, and_1_out);
  and and_6 (and_6_out, A1, and_1_out);
  and and_7 (and_7_out, A0, and_1_out);
  and and_8 (and_8_out, B2, and_1_out);
  and and_9 (and_9_out, B1, and_1_out);
  and and_10 (and_10_out, B0, and_1_out);
  and and_11 (and_11_out, A2, and_2_out);
  and and_12 (and_12_out, A1, and_2_out);
  and and_13 (and_13_out, A0, and_2_out);
  and and_14 (and_14_out, B2, and_2_out);
  and and_15 (and_15_out, B1, and_2_out);
  and and_16 (and_16_out, B0, and_2_out);
  and and_17 (and_17_out, A2, and_3_out);
  and and_18 (and_18_out, A1, and_3_out);
  and and_19 (and_19_out, A0, and_3_out);
  and and_20 (and_20_out, B2, and_3_out);
  and and_21 (and_21_out, B1, and_3_out);
  and and_22 (and_22_out, B0, and_3_out);
  and and_23 (and_23_out, A2, and_4_out);
  and and_24 (and_24_out, A1, and_4_out);
  and and_25 (and_25_out, A0, and_4_out);
  and and_26 (and_26_out, B2, and_4_out);
  and and_27 (and_27_out, B1, and_4_out);
  and and_28 (and_28_out, B0, and_4_out);
  or or_1 (or_1_out, and_5_out, and_11_out, and_17_out, and_23_out);
  or or_2 (or_2_out, and_6_out, and_12_out, and_18_out, and_24_out);
  Seven_Seg seven_seg_1 (.a(1'b0), .b(1'b0), .c(1'b0), .d(1'b0), .e(1'b0), .f(1'b0), .g(or_1_out), .dp(1'b0));
  Seven_Seg seven_seg_2 (
    .a(display_entrada_a_1_d4), .b(display_entrada_a_1_d2), .c(display_entrada_a_1_d3),
    .d(display_entrada_a_1_d1), .e(display_entrada_a_1_d5), .f(display_entrada_a_1_d6),
    .g(display_entrada_a_1_d7), .dp(1'b0));
  or or_3 (or_3_out, and_7_out, and_13_out, and_19_out, and_25_out);
  or or_4 (or_4_out, and_8_out, and_14_out, and_20_out, and_26_out);
  Seven_Seg seven_seg_3 (.a(1'b0), .b(1'b0), .c(1'b0), .d(1'b0), .e(1'b0), .f(1'b0), .g(or_4_out), .dp(1'b0));
  DISPLAY_ENTRADA_B display_entrada_b_1 (
    .Codi(Codi), .B2(or_4_out), .B1(or_5_out), .B0(or_6_out), .d1(display_entrada_b_1_d1),
    .d2(display_entrada_b_1_d2), .d3(display_entrada_b_1_d3), .d4(display_entrada_b_1_d4),
    .d5(display_entrada_b_1_d5), .d6(display_entrada_b_1_d6), .d7(display_entrada_b_1_d7));
  or or_5 (or_5_out, and_9_out, and_15_out, and_21_out, and_27_out);
  Seven_Seg seven_seg_4 (
    .a(display_entrada_b_1_d1), .b(display_entrada_b_1_d2), .c(display_entrada_b_1_d3),
    .d(display_entrada_b_1_d4), .e(display_entrada_b_1_d5), .f(display_entrada_b_1_d6),
    .g(display_entrada_b_1_d7), .dp(1'b0));
  or or_6 (or_6_out, and_10_out, and_16_out, and_22_out, and_28_out);
  Suma_C2 suma_c2_1 (
    .A0(and_7_out), .B0(and_10_out), .A1(and_6_out), .B1(and_9_out), .A2(and_5_out), .B2(and_8_out),
    .R0(suma_c2_1_r0), .R1(suma_c2_1_r1), .R2(suma_c2_1_r2), .C(suma_c2_1_c), .O(suma_c2_1_o));
  Suma_SM suma_sm_1 (
    .A2(and_11_out), .A1(and_12_out), .A0(and_13_out), .B2(and_14_out), .B1(and_15_out), .B0(and_16_out),
    .O(suma_sm_1_o), .C(suma_sm_1_c), .R2(suma_sm_1_r2), .R1(suma_sm_1_r1), .R0(suma_sm_1_r0));
  Resta_C2 resta_c2_1 (
    .A0(and_19_out), .B0(and_22_out), .A1(and_18_out), .B1(and_21_out), .B2(and_20_out), .A2(and_17_out),
    .R0(resta_c2_1_r0), .R1(resta_c2_1_r1), .Cout(resta_c2_1_cout), .R2(resta_c2_1_r2), .Ov(resta_c2_1_ov));
  Resta_SM resta_sm_1 (
    .A2(and_23_out), .A1(and_24_out), .A0(and_25_out), .B2(and_26_out), .B1(and_27_out), .B0(and_28_out),
    .O(resta_sm_1_o), .C(resta_sm_1_c), .R2(resta_sm_1_r2), .R1(resta_sm_1_r1), .R0(resta_sm_1_r0));
  or or_7 (R0, suma_c2_1_r0, suma_sm_1_r0, resta_c2_1_r0, resta_sm_1_r0);
  or or_8 (R1, suma_c2_1_r1, suma_sm_1_r1, resta_c2_1_r1, resta_sm_1_r1);
  or or_9 (R2, suma_c2_1_r2, suma_sm_1_r2, resta_c2_1_r2, resta_sm_1_r2);
  or or_10 (out_9, suma_c2_1_c, suma_sm_1_c, resta_c2_1_cout, resta_sm_1_c);
  or or_11 (out_10, suma_sm_1_o, suma_c2_1_o, resta_c2_1_ov, resta_sm_1_o);
  DISPLAY_RESULTADO display_resultado_1 (
    .Codi(Codi), .R2(R2), .R1(R1), .R0(R0), .d1(display_resultado_1_d1), .d2(display_resultado_1_d2),
    .d3(display_resultado_1_d3), .d4(display_resultado_1_d4), .d5(display_resultado_1_d5),
    .d6(display_resultado_1_d6), .d7(display_resultado_1_d7));
  Seven_Seg seven_seg_5 (.a(1'b0), .b(1'b0), .c(1'b0), .d(1'b0), .e(1'b0), .f(1'b0), .g(R2), .dp(1'b0));
  Seven_Seg seven_seg_6 (
    .a(display_resultado_1_d1), .b(display_resultado_1_d2), .c(display_resultado_1_d3),
    .d(display_resultado_1_d4), .e(display_resultado_1_d5), .f(display_resultado_1_d6),
    .g(display_resultado_1_d7), .dp(1'b0));

  // Other names for the same wires on the sheet: _1 = R0; _2 = R1; _3 = R2

  // Notes on the sheet:
  //   DEMUX CON ENTRADAS OP I CODI 
  //   PARA SELECCIONAR OPERACIÓN
  //   A2
  //   A1
  //   A0
  //   B2
  //   B1
  //   B0
  //   OPERANDO A
  //   OPERANDO B
  //   R0
  //   R1
  //   R2
  //   C
  //   O
  //   Carry Out
  //   Overflow
  //   RESULTADO
endmodule
