// Digital circuit Resta SM.dig as structural Verilog
module Resta_SM (
  input  A2,
  input  A1,
  input  A0,
  input  B2,
  input  B1,
  input  B0,
  output O,
  output C,
  output R2,
  output R1,
  output R0
);

  wire nand_1_out, nand_2_out, nand_3_out, nand_4_out, nand_5_out, nand_6_out, nand_7_out, nand_8_out,
       nand_9_out, nand_10_out, nand_11_out, nand_12_out, nand_13_out, nand_14_out, nand_15_out, nand_16_out,
       nand_17_out, nand_18_out, nand_19_out, nand_20_out, nand_21_out, nand_22_out, nand_23_out,
       nand_24_out, nand_25_out, nand_26_out, nand_27_out, nand_28_out, nand_29_out, nand_30_out,
       nand_31_out, nand_32_out, nand_33_out, nand_34_out, not_1_out, not_2_out, not_3_out, not_4_out,
       not_5_out, not_6_out;

  not not_1 (not_1_out, A2);
  not not_2 (not_2_out, A1);
  not not_3 (not_3_out, A0);
  not not_4 (not_4_out, B2);
  not not_5 (not_5_out, B1);
  not not_6 (not_6_out, B0);
  nand nand_1 (nand_1_out, A0, not_1_out, B0, B1, B2);
  nand nand_2 (nand_2_out, A0, A2, B0, B1, not_4_out);
  nand nand_3 (nand_3_out, A0, A1, not_1_out, B0, B2);
  nand nand_4 (nand_4_out, A0, A1, A2, B0, not_4_out);
  nand nand_5 (nand_5_out, A1, not_1_out, B1, B2);
  nand nand_6 (nand_6_out, A1, A2, B1, not_4_out);
  nand nand_7 (nand_7_out, A0, not_1_out, B0, B1, B2);
  nand nand_8 (nand_8_out, A0, A2, B0, B1, not_4_out);
  nand nand_9 (nand_9_out, A0, A1, not_1_out, B0, B2);
  nand nand_10 (nand_10_out, A0, A1, A2, B0, not_4_out);
  nand nand_11 (nand_11_out, A1, not_1_out, B1, B2);
  nand nand_12 (nand_12_out, A1, A2, B1, not_4_out);
  nand nand_13 (nand_13_out, not_2_out, B0, not_4_out);
  nand nand_14 (nand_14_out, A1, A2, not_6_out);
  nand nand_15 (nand_15_out, not_2_out, B1, not_4_out);
  nand nand_16 (nand_16_out, A1, A2, not_5_out);
  nand nand_17 (nand_17_out, A2, not_6_out, not_5_out);
  nand nand_18 (nand_18_out, B0, B1, not_4_out);
  nand nand_19 (nand_19_out, A0, not_2_out, not_1_out, B0, not_5_out, B2);
  nand nand_20 (nand_20_out, A0, A1, not_1_out, B0, B1, B2);
  nand nand_21 (nand_21_out, A0, not_2_out, A2, B0, not_5_out, not_4_out);
  nand nand_22 (nand_22_out, A0, A1, A2, B0, B1, not_4_out);
  nand nand_23 (nand_23_out, not_3_out, A1, not_1_out, not_5_out, B2);
  nand nand_24 (nand_24_out, A0, A1, not_1_out, not_5_out, not_4_out);
  nand nand_25 (nand_25_out, not_3_out, A1, A2, not_5_out, not_4_out);
  nand nand_26 (nand_26_out, A0, A1, A2, not_5_out, B2);
  nand nand_27 (nand_27_out, not_3_out, not_2_out, B1);
  nand nand_28 (nand_28_out, not_2_out, not_1_out, B0, B1, not_4_out);
  nand nand_29 (nand_29_out, not_2_out, not_1_out, not_6_out, B1, B2);
  nand nand_30 (nand_30_out, not_2_out, A2, not_6_out, B1, not_4_out);
  nand nand_31 (nand_31_out, not_2_out, A2, B0, B1, B2);
  nand nand_32 (nand_32_out, A1, not_6_out, not_5_out);
  nand nand_33 (nand_33_out, not_3_out, B0);
  nand nand_34 (nand_34_out, A0, not_6_out);
  nand nand_35 (R0, nand_33_out, nand_34_out);
  nand nand_36 (O, nand_1_out, nand_2_out, nand_3_out, nand_4_out, nand_5_out, nand_6_out);
  nand nand_37 (C, nand_7_out, nand_8_out, nand_9_out, nand_10_out, nand_11_out, nand_12_out);
  nand nand_38 (R2, nand_13_out, nand_14_out, nand_15_out, nand_16_out, nand_17_out, nand_18_out);
  nand nand_39 (R1, nand_19_out, nand_20_out, nand_21_out, nand_22_out, nand_23_out, nand_24_out, nand_25_out, nand_26_out, nand_27_out, nand_28_out, nand_29_out, nand_30_out, nand_31_out, nand_32_out);
endmodule
