// Digital circuit Suma C2.dig as structural Verilog
module Suma_C2 (
  input  A0,
  input  B0,
  input  A1,
  input  B1,
  input  A2,
  input  B2,
  output R0,
  output R1,
  output R2,
  output C,
  output O
);

  wire and_1_out, and_2_out, and_3_out, and_4_out, and_5_out, and_6_out, or_1_out, or_2_out, xor_1_out,
       xor_3_out, xor_5_out, xor_6_out, xor_7_out;

  xor xor_1 (xor_1_out, A0, B0);
  and and_1 (and_1_out, A0, B0);
  and and_2 (and_2_out, 1'b0, xor_1_out);
  xor xor_2 (R0, xor_1_out, 1'b0);
  or or_1 (or_1_out, and_2_out, and_1_out);
  xor xor_3 (xor_3_out, A1, B1);
  and and_3 (and_3_out, A1, B1);
  and and_4 (and_4_out, or_1_out, xor_3_out);
  xor xor_4 (R1, xor_3_out, or_1_out);
  or or_2 (or_2_out, and_4_out, and_3_out);
  xor xor_5 (xor_5_out, A2, R2);
  xor xor_6 (xor_6_out, R2, B2);
  xor xor_7 (xor_7_out, A2, B2);
  and and_5 (and_5_out, A2, B2);
  and and_6 (and_6_out, or_2_out, xor_7_out);
  and and_7 (O, xor_5_out, xor_6_out);
  xor xor_8 (R2, xor_7_out, or_2_out);
  or or_3 (C, and_6_out, and_5_out);

  // Notes on the sheet:
  //   C
endmodule
